// Logisim project alu.circ as structural Verilog: 1 circuit, main circuit alu
module alu (
  input  [31:0] A,
  input  [31:0] B,
  input  [3:0] ALUSel,
  output [31:0] Result
);

  wire adder_1_cout, comparator_1_lt;
  wire [31:0] add0, and0, mul0, mulh0, mulhu0, multiplier_2_out, multiplier_3_out, or0, sll0, slt0, sra0,
       srl0, sub0, xor0;
  wire [63:0] bit_extender_1_out, bit_extender_2_out, bit_extender_4_out, bit_extender_5_out;

  assign bit_extender_1_out = {{32{1'b0}}, A};  // Bit_Extender bit_extender_1
  assign bit_extender_2_out = {{32{A[31]}}, A};  // Bit_Extender bit_extender_2
  Adder #(.width(32)) adder_1 (.a(A), .b(B), .out(add0), .cout(adder_1_cout));  // open: cin
  assign and0 = A & B;  // AND_Gate and_1, 32 bits wide
  assign or0 = A | B;  // OR_Gate or_1, 32 bits wide
  assign xor0 = A ^ B;  // XOR_Gate xor_1, 32 bits wide
  Shifter #(.shift("lr"), .width(32)) shifter_1 (.in(A), .\dist (B[4:0]), .out(srl0));
  Shifter #(.shift("ar"), .width(32)) shifter_2 (.in(A), .\dist (B[4:0]), .out(sra0));
  Shifter #(.width(32)) shifter_3 (.in(A), .\dist (B[4:0]), .out(sll0));
  Comparator #(.width(32)) comparator_1 (.a(A), .b(B), .lt(comparator_1_lt));  // open: gt, eq
  assign slt0 = {{31{1'b0}}, comparator_1_lt};  // Bit_Extender bit_extender_3
  Multiplier #(.width(32)) multiplier_1 (.a(A), .b(B), .out(mul0));  // open: cin, cout
  Multiplier #(.mode("twosComplement"), .width(64)) multiplier_2 (
    .a(bit_extender_1_out), .b(bit_extender_4_out), .out({mulhu0, multiplier_2_out}));  // open: cin, cout
  assign bit_extender_4_out = {{32{1'b0}}, B};  // Bit_Extender bit_extender_4
  Subtractor #(.width(32)) subtractor_1 (.a(A), .b(B), .out(sub0));  // open: bin, bout
  Multiplier #(.mode("twosComplement"), .width(64)) multiplier_3 (
    .a(bit_extender_2_out), .b(bit_extender_5_out), .out({mulh0, multiplier_3_out}));  // open: cin, cout
  assign bit_extender_5_out = {{32{B[31]}}, B};  // Bit_Extender bit_extender_5
  Multiplexer #(.enable("false"), .select(4), .width(32)) multiplexer_1 (
    .in0(add0), .in1(and0), .in2(or0), .in3(xor0), .in4(srl0), .in5(sra0), .in6(sll0), .in7(slt0),
    .in10(mul0), .in11(mulhu0), .in12(sub0), .in13(B), .in14(mulh0), .out(Result), .sel(ALUSel));  // open: in8, in9, in15

  // Other names for the same wires on the sheet: bsel0[31:0] = B

  // Notes on the sheet:
  //   INPUTS to your circuit
  //   DON'T CHANGE THE LOCATIONS OF THE INPUTS AND OUTPUTS!
  //   OUTPUT from your circuit
endmodule
