// Logisim project control_logic.circ as structural Verilog: 1 circuit, main circuit control_logic
module control_logic (
  input  [31:0] inst,
  input  BrEq,
  input  BrLt,
  output PCSel,
  output RegWEn,
  output [2:0] ImmSel,
  output BrUn,
  output ASel,
  output BSel,
  output [3:0] ALUSel,
  output MemRW,
  output [1:0] WBSel,
  output CSRSel,
  output CSRWen
);

  wire and_4_out, and_5_out, and_6_out, and_7_out, and_8_out, and_10_out, and_11_out, and_12_out, and_13_out,
       and_14_out, and_15_out, and_16_out, and_17_out, and_18_out, and_19_out, and_20_out, and_21_out,
       and_22_out, auipc, branch_satisfied, decoder_3_out0, decoder_3_out1, decoder_4_out0, decoder_4_out1,
       funct3_0, funct3_1, funct3_2, funct3_3, funct3_4, funct3_6, funct3_7, funct7_00, funct7_01, funct7_20,
       i_type, jalr, nor_2_out, opcode_0x03, opcode_0x6f, opcode_0x13, opcode_0x33, opcode_0x37, opcode_0x63,
       or_3_out, or_4_out, or_5_out, or_6_out, or_10_out, or_11_out, or_12_out, or_13_out, or_14_out,
       or_15_out, or_16_out, u_type;

  Decoder #(.select(5)) decoder_1 (
    .out0(opcode_0x03), .out4(opcode_0x13), .out5(auipc), .out8(MemRW), .out12(opcode_0x33),
    .out13(opcode_0x37), .out24(opcode_0x63), .out25(jalr), .out27(opcode_0x6f), .out28(CSRWen),
    .sel(inst[6:2]));  // open: out1, out2, out3, out6, out7, out9, out10, out11, out14, out15, out16, out17, out18, out19, out20, out21, out22, out23, out26, out29, out30, out31, en
  Decoder #(.select(3)) decoder_2 (
    .out0(funct3_0), .out1(funct3_1), .out2(funct3_2), .out3(funct3_3), .out4(funct3_4), .out5(CSRSel),
    .out6(funct3_6), .out7(funct3_7), .sel(inst[14:12]));  // open: en
  Decoder #(.select(2)) decoder_3 (
    .out0(decoder_3_out0), .out1(decoder_3_out1), .sel(inst[31:30]));  // open: out2, out3, en
  Decoder #(.select(5)) decoder_4 (
    .out0(decoder_4_out0), .out1(decoder_4_out1), .sel(inst[29:25]));  // open: out2, out3, out4, out5, out6, out7, out8, out9, out10, out11, out12, out13, out14, out15, out16, out17, out18, out19, out20, out21, out22, out23, out24, out25, out26, out27, out28, out29, out30, out31, en
  or or_1 (i_type, opcode_0x03, opcode_0x13, jalr, CSRWen);
  or or_2 (u_type, auipc, opcode_0x37);
  and and_1 (funct7_00, decoder_3_out0, decoder_4_out0);
  and and_2 (funct7_01, decoder_3_out0, decoder_4_out1);
  and and_3 (funct7_20, decoder_3_out1, decoder_4_out0);
  or or_3 (or_3_out, funct3_4, funct3_6);
  or or_4 (or_4_out, CSRSel, funct3_7);
  and and_4 (and_4_out, BrEq, funct3_0);
  and and_5 (and_5_out, ~BrEq, funct3_1);  // AND_Gate
  and and_6 (and_6_out, BrLt, or_3_out);
  and and_7 (and_7_out, ~BrLt, or_4_out);  // AND_Gate
  and and_8 (and_8_out, branch_satisfied, opcode_0x63);
  or or_5 (or_5_out, funct3_6, funct3_7);
  not not_1 (BSel, opcode_0x33);
  or or_6 (or_6_out, opcode_0x6f, jalr);
  or or_7 (branch_satisfied, and_4_out, and_5_out, and_6_out, and_7_out);
  or or_8 (PCSel, and_8_out, opcode_0x6f, jalr);
  nor nor_1 (RegWEn, MemRW, opcode_0x63);
  Priority_Encoder priority_encoder_1 (
    .in0(i_type), .in1(MemRW), .in2(opcode_0x63), .in3(u_type), .in4(opcode_0x6f), .out(ImmSel));  // open: in5, in6, in7, en_in, gs, en_out
  and and_9 (BrUn, opcode_0x63, or_5_out);
  or or_9 (ASel, opcode_0x63, auipc, opcode_0x6f);
  nor nor_2 (nor_2_out, opcode_0x03, or_6_out);
  Priority_Encoder #(.select(2)) priority_encoder_2 (
    .in0(opcode_0x03), .in1(nor_2_out), .in2(or_6_out), .out(WBSel));  // open: in3, gs, en_out, en_in
  or or_10 (or_10_out, i_type, opcode_0x33);
  or or_11 (or_11_out, i_type, opcode_0x33);
  or or_12 (or_12_out, i_type, opcode_0x33);
  or or_13 (or_13_out, i_type, opcode_0x33);
  and and_10 (and_10_out, or_13_out, CSRSel);
  and and_11 (and_11_out, opcode_0x33, funct3_0);
  and and_12 (and_12_out, or_10_out, funct3_7);
  and and_13 (and_13_out, or_11_out, funct3_6);
  and and_14 (and_14_out, or_12_out, funct3_4);
  and and_15 (and_15_out, funct7_00, and_10_out);
  and and_16 (and_16_out, and_10_out, funct7_20);
  or or_14 (or_14_out, i_type, opcode_0x33);
  and and_17 (and_17_out, or_14_out, funct3_1, funct7_00);
  or or_15 (or_15_out, opcode_0x13, opcode_0x33);
  and and_18 (and_18_out, or_15_out, funct3_2);
  and and_19 (and_19_out, and_11_out, funct7_01);
  and and_20 (and_20_out, and_11_out, funct7_20);
  and and_21 (and_21_out, opcode_0x33, funct3_3, funct7_01);
  or or_16 (or_16_out, MemRW, CSRWen);
  and and_22 (and_22_out, opcode_0x33, funct3_1, funct7_01);
  Priority_Encoder #(.select(4)) priority_encoder_3 (
    .in0(1'b1), .in1(and_12_out), .in2(and_13_out), .in3(and_14_out), .in4(and_15_out), .in5(and_16_out),
    .in6(and_17_out), .in7(and_18_out), .in10(and_19_out), .in11(and_21_out), .in12(and_20_out),
    .in13(or_16_out), .in14(and_22_out), .out(ALUSel));  // open: in8, in9, in15, gs, en_out, en_in

  // Other names for the same wires on the sheet: funct3_5 = CSRSel; opcode[6:0] = inst[6:0];
  //   funct3[2:0] = inst[14:12]; funct7[6:0] = inst[31:25]; opcode_0x17 = auipc; opcode_0x67 = jalr; csr = CSRWen;
  //   opcode_0x73 = CSRWen; r_type = opcode_0x33; opcode_0x23 = MemRW; s_type = MemRW; sb_type = opcode_0x63;
  //   uj_type = opcode_0x6f

  // Notes on the sheet:
  //   INPUTS to your circuit
  //   DON'T CHANGE THE LOCATIONS OF THE INPUTS AND OUTPUTS!
  //   OUTPUT from your circuit
endmodule
