// Logisim project csr.circ as structural Verilog: 1 circuit, main circuit csr
module csr (
  input  [11:0] CSR_address,
  input  [31:0] CSR_din,
  input  CSR_WE,
  input  clk,
  output [31:0] tohost
);

  wire [31:0] ram_1_dout;

  RAM #(.addrWidth(12), .dataWidth(32)) ram_1 (
    .addr(CSR_address), .we(CSR_WE), .oe(1'b1), .clk(clk), .din(CSR_din), .dout(ram_1_dout));
  Register #(.width(32)) register_1 (.D(CSR_din), .en(CSR_WE), .clk(clk), .Q(tohost));  // open: clr

  // Other names for the same wires on the sheet: address[11:0] = CSR_address; data[31:0] = CSR_din; WE = CSR_WE

  // Notes on the sheet:
  //   INPUTS to your circuit
  //   DON'T CHANGE THE LOCATIONS OF THE INPUTS AND OUTPUTS!
  //   OUTPUT from your circuit
endmodule
